// Logisim project HW_4.circ as structural Verilog: 1 circuit, main circuit main
module main (
  input  w,
  input  x,
  input  y,
  input  z,
  output f
);

  wire and_1_out, and_2_out, and_3_out, and_4_out, not_1_out, not_2_out, not_3_out, not_4_out;

  not not_1 (not_1_out, x);
  and and_1 (and_1_out, not_1_out, y, not_2_out);
  not not_2 (not_2_out, z);
  not not_3 (not_3_out, w);
  and and_2 (and_2_out, not_3_out, y, z);
  and and_3 (and_3_out, w, x, not_4_out);
  not not_4 (not_4_out, y);
  and and_4 (and_4_out, w, x, z);
  or or_1 (f, and_1_out, and_2_out, and_3_out, and_4_out);
endmodule
